// Logisim project cpu.circ as structural Verilog: 1 circuit, main circuit cpu
module cpu (
  input  clk,
  input  [31:0] INSTRUCTION,
  input  [31:0] READ_DATA,
  output [31:0] WRITE_ADDRESS,
  output [31:0] PROGRAM_COUNTER,
  output [31:0] ra,
  output [31:0] sp,
  output [31:0] t0,
  output [31:0] t1,
  output [31:0] t2,
  output [31:0] s0,
  output [31:0] s1,
  output [31:0] a0,
  output [31:0] tohost,
  output [3:0] WRITE_ENABLE,
  output [31:0] WRITE_DATA
);

  wire BSel, control_logic_1_regwen;
  wire [2:0] control_logic_1_immsel, funct3;
  wire [3:0] ALUSel;
  wire [6:0] funct7;
  wire [24:0] inst_2s;
  wire [31:0] adder_1_out, alu_1_result, imm, multiplexer_1_out, regfile_1_read_data_1, regfile_1_read_data_2;

  Adder #(.width(32)) adder_1 (.a(PROGRAM_COUNTER), .b(32'h4), .out(adder_1_out));  // open: cin, cout
  Register #(.width(32)) PC (.D(adder_1_out), .en(1'b1), .clk(clk), .Q(PROGRAM_COUNTER));  // open: clr
  Register #(.width(32)) register_1 (
    .D(INSTRUCTION), .en(1'b1), .clk(clk), .Q({funct7, inst_2s[24:15], funct3, inst_2s[11:0]}));  // open: clr
  imm_gen imm_gen_1 (
    .inst({funct7, inst_2s[24:15], funct3, inst_2s[11:0]}), .ImmSel(control_logic_1_immsel), .imm(imm));
  control_logic control_logic_1 (
    .RegWEn(control_logic_1_regwen), .ImmSel(control_logic_1_immsel), .BSel(BSel), .ALUSel(ALUSel),
    .inst({funct7, inst_2s[24:15], funct3, inst_2s[11:0]}));  // open: CSRWen, PCSel, BrUn, ASel, MemRW, WBSel, CSRSel, BrEq, BrLt
  regfile regfile_1 (
    .rs1(inst_2s[19:15]), .rs2(inst_2s[24:20]), .rd(inst_2s[11:7]), .Write_Data(alu_1_result),
    .RegWEn(control_logic_1_regwen), .clk(clk), .ra(ra), .sp(sp), .t0(t0), .t1(t1), .t2(t2), .s0(s0),
    .s1(s1), .a0(a0), .Read_Data_1(regfile_1_read_data_1), .Read_Data_2(regfile_1_read_data_2));
  // branch_comp branch_comp_1: pin names not known
  Multiplexer #(.enable("false"), .width(32)) multiplexer_1 (
    .in0(regfile_1_read_data_2), .in1(imm), .out(multiplexer_1_out), .sel(BSel));
  alu alu_1 (.Result(alu_1_result), .A(regfile_1_read_data_1), .B(multiplexer_1_out), .ALUSel(ALUSel));
  csr csr_1 (.tohost(tohost));  // open: CSR_address, CSR_din, CSR_WE, clk

  // Other names for the same wires on the sheet: opcode[6:0] = inst_2s[6:0]; rd[4:0] = inst_2s[11:7];
  //   inst_2s (some bits) = {funct7, funct3}; rs1[4:0] = inst_2s[19:15]; rs2[4:0] = inst_2s[24:20]

  // Notes on the sheet:
  //   Output to IMEM
  //   IMEM (do **NOT** move this)
  //   Inputs from IMEM
  //   Inputs/Outputs for testing. Do **NOT** move these.
  //   Outputs To DMEM
  //   DMEM (do **NOT** move this)
  //   Inputs From DMEM
endmodule
